# Fritzing sketch MotorFritzingWIP (saved by Fritzing 0.9.3b)
breadboards: 1

parts:
  Part1 = Arduino Uno (Rev3)
  VCC1 = Battery
  D1 = Diode [package=diode-1n4148]  # not connected

nets:
  N1: Part1.GND, VCC1.-
